# Fritzing sketch Leaf&Soil (saved by Fritzing 0.9.4)
breadboards: 1

parts:
  U2 = NodeMCU V1.0
  Capacitive_Soil_Moisture_Sensor2 = DFRobot Capacitive Soil Moisture Sensor V1.0 [part_number=SEN0193]
  Part2 = Adafruit ADS1115 16Bit I2C ADC [part_number="Adafruit #1085"]
  YL-83_-_Detection_Board2 = YL-83 Rain Sensor - Detection Board
  YL-83_-_Control_Board2 = YL-83 Rain Sensor - Control Board

nets:
  N1: U2.D1, Part2.SCL
  N2: U2.D2, Part2.SDA
  VCC: U2.3V3, Capacitive_Soil_Moisture_Sensor2.VCC, Part2.VDD, YL-83_-_Control_Board2.VCC
  GND: U2.GND, Capacitive_Soil_Moisture_Sensor2.GND, Part2.ADDR, Part2.GND, YL-83_-_Control_Board2.GND
  N3: U2.A0, YL-83_-_Control_Board2.AO
  N4: Capacitive_Soil_Moisture_Sensor2.A, Part2.AIN2
  N5: YL-83_-_Detection_Board2.POS, YL-83_-_Control_Board2.POS
  N6: YL-83_-_Detection_Board2.NEG, YL-83_-_Control_Board2.NEG

notes:
  Infi-Leaf
  Leaf Wetness Sensor

custom parts:
  NodeMCU V1.0: ESP8266 based NodeMCU
  DFRobot Capacitive Soil Moisture Sensor V1.0: DFRobot Capacitive Soil Moisture Sensor V1.0 This product measures soil moisture levels by capacitive sensing, rather than resistive sensing like other types of moisture sensor. It is made of a corrosion resistant material giving it a long service life. Insert it into soil and impress your friends with the real-time soil moisture data! The product includes an on-board voltage regulator which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
  Adafruit ADS1115 16Bit I2C ADC: For microcontrollers without an analog-to-digital converter or when you want a higher-precision ADC, the ADS1115 provides 16-bit precision at 860 samples/second over I2C. The chip can be configured as 4 single-ended input channels, or two differential channels. As a nice bonus, it even includes a programmable gain amplifier, up to x16, to help boost up smaller single/differential signals to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
  YL-83 Rain Sensor - Detection Board: The YL-83 is a rain sensor that has more resistance when dry and less resistance when wet. The module runs at 5V.
  YL-83 Rain Sensor - Control Board: The YL-83 is a rain sensor that has more resistance when dry and less resistance when wet. The module runs at 5V.
