# Fritzing sketch button&LED (saved by Fritzing 0.9.4)
breadboards: 1

parts:
  U1 = NodeMCU V1.0
  LED1 = smd LED [color="Red (633nm)" package="0603 [SMD]"]
  S1 = Pushbutton [package="[THT]"]
  C1 = Ceramic Capacitor [capacitance=100nF package="200 mil [THT, multilayer]"]
  R1 = Resistor [tolerance=±5% resistance=220 package="0402 [SMD]"]

nets:
  N1: U1.D4, S1.Pin_3, S1.Pin_4, C1.0
  N2: U1.GND, LED1.cathode, S1.Pin_1, S1.Pin_2, C1.1
  N3: U1.D6, R1.Pin_0
  N4: LED1.anode, R1.Pin_1

notes:
  .1uF Ceramic Capacitor

custom parts:
  NodeMCU V1.0: ESP8266 based NodeMCU
