# Fritzing sketch soil_moisture+soil_temp' (saved by Fritzing 0.9.4)
breadboards: 1

parts:
  U1 = NodeMCU V1.0
  part = DS18B20 1-Wire Temperature Sensor Module [part_number=DS18B20]
  Capacitive_Soil_Moisture_Sensor1 = DFRobot Capacitive Soil Moisture Sensor V1.0 [part_number=SEN0193]
  Part1 = Adafruit ADS1115 16Bit I2C ADC [part_number="Adafruit #1085"]

nets:
  N1: U1.D1, Part1.SCL
  N2: U1.D2, Part1.SDA
  VDD: U1.3V3, part.VDD, Capacitive_Soil_Moisture_Sensor1.VCC, Part1.VDD
  GND: U1.GND, part.GND, Capacitive_Soil_Moisture_Sensor1.GND, Part1.ADDR, Part1.GND
  N3: U1.D6, part.OUT
  N4: Capacitive_Soil_Moisture_Sensor1.A, Part1.AIN0

custom parts:
  NodeMCU V1.0: ESP8266 based NodeMCU
  DS18B20 1-Wire Temperature Sensor Module: DS18B20 1-Wire Temperature Sensor Module The DS18B20 digital thermometer provides 9-bit to 12-bit Celsius temperature measurements and has an alarm function with nonvolatile user-programmable upper and lower trigger points. The DS18B20 communicates over a 1-Wire bus that by definition requires only one data line (and ground) for communication with a central microprocessor. In addition, the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
  DFRobot Capacitive Soil Moisture Sensor V1.0: DFRobot Capacitive Soil Moisture Sensor V1.0 This product measures soil moisture levels by capacitive sensing, rather than resistive sensing like other types of moisture sensor. It is made of a corrosion resistant material giving it a long service life. Insert it into soil and impress your friends with the real-time soil moisture data! The product includes an on-board voltage regulator which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
  Adafruit ADS1115 16Bit I2C ADC: For microcontrollers without an analog-to-digital converter or when you want a higher-precision ADC, the ADS1115 provides 16-bit precision at 860 samples/second over I2C. The chip can be configured as 4 single-ended input channels, or two differential channels. As a nice bonus, it even includes a programmable gain amplifier, up to x16, to help boost up smaller single/differential signals to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
